// Logisim project ULA.circ as structural Verilog: 25 circuits, main circuit main
module main (
  input  _0,
  input  _0_2,
  input  [2:0] in_3,
  input  in_4,
  input  in_5,
  input  _1,
  input  _1_2,
  input  in_8,
  input  in_9,
  input  _0_3,
  input  _1_3,
  input  in_12,
  input  in_13,
  input  [4:0] _01010,
  input  [4:0] _01010_2,
  input  [4:0] A,
  input  _1_4,
  input  [4:0] B,
  input  in_19,
  input  in_20,
  input  _1_5,
  input  [4:0] aux,
  input  _1_6,
  input  in_24,
  input  in_25,
  input  _0_4,
  input  _1_7,
  input  _1_8,
  input  _1_9,
  input  in_30,
  input  _0_5,
  input  _0_6,
  output [4:0] out_33
);

  wire _5bit_comparator_a___b, _5bt_comparator_a___b, _5it_comparator_a___b, _7_decoder_2_a_2,
       _7_decoder_2_b_2, _7_decoder_2_c_2, _7_decoder_2_d_2, _7_decoder_2_e, _7_decoder_2_f, _7_decoder_2_g,
       _7_decoder_a_2, _7_decoder_b_2, _7_decoder_c_2, _7_decoder_d_2, _7_decoder_e, _7_decoder_f,
       _7_decoder_g, _7decoder_2_a_2, _7decoder_2_b_2, _7decoder_2_c_2, _7decoder_2_d_2, _7decoder_2_e,
       _7decoder_2_f, _7decoder_2_g, _7decoder_3_a_2, _7decoder_3_b_2, _7decoder_3_c_2, _7decoder_3_d_2,
       _7decoder_3_e, _7decoder_3_f, _7decoder_3_g, _7decoder_a_2, _7decoder_b_2, _7decoder_c_2,
       _7decoder_d_2, _7decoder_e, _7decoder_f, _7decoder_g, adder_overflow, and_1_out, and_2_out, and_3_out,
       and_4_out, and_5_out, and_6_out, greater_than_out_6, less_or_equal_to_out_7, multiplier_1_overflow,
       n7_segment_decoder_1_a_2, n7_segment_decoder_1_b_2, n7_segment_decoder_1_c_2,
       n7_segment_decoder_1_d_2, n7_segment_decoder_1_e, n7_segment_decoder_1_f, n7_segment_decoder_1_g,
       not_1_out, not_2_out, not_3_out, not_4_out, not_5_out, not_6_out, not_7_out, or_1_out, or_2_out,
       subtractor_overflow;
  wire [4:0] _2x1_mult_2_out_4, _2x1_mult_out_4, _5bit_sub_output, _5bit_subtractor_output, _8x1_mult_out_10,
       adder_output, C2_format_2_output, C2_format_output, greater_than_output, less_or_equal_to_output,
       min_out_6, multiplier_1_output, shift_bit_n_times_1_output, subtractor_2_output, subtractor_output;

  _7_Segment_Display u_7_segment_display_1 (
    .g(_7decoder_g), .f(_7decoder_f), .a(_7decoder_a_2), .b(_7decoder_b_2), .e(_7decoder_e),
    .d(_7decoder_d_2), .c(_7decoder_c_2));  // open: dp
  _7_Segment_Display u_7_segment_display_2 (
    .g(_7decoder_3_g), .f(_7decoder_3_f), .a(_7decoder_3_a_2), .b(_7decoder_3_b_2), .e(_7decoder_3_e),
    .d(_7decoder_3_d_2), .c(_7decoder_3_c_2));  // open: dp
  _7_segment_decoder _7decoder (
    .A(_0_2), .B(_0_2), .C(_0_2), .D(not_1_out), .a_2(_7decoder_a_2), .b_2(_7decoder_b_2),
    .c_2(_7decoder_c_2), .d_2(_7decoder_d_2), .e(_7decoder_e), .f(_7decoder_f), .g(_7decoder_g));
  not not_1 (not_1_out, _5it_comparator_a___b);
  _5bit_subtractor _5bit_sub (.\output (_5bit_sub_output), .m(_1_7), .A(B), .B(_01010_2));  // open: Overflow
  not not_2 (not_2_out, _5bit_comparator_a___b);
  _7_segment_decoder _7decoder_2 (
    .A(_0_6), .B(_0_6), .C(_0_6), .D(not_2_out), .a_2(_7decoder_2_a_2), .b_2(_7decoder_2_b_2),
    .c_2(_7decoder_2_c_2), .d_2(_7decoder_2_d_2), .e(_7decoder_2_e), .f(_7decoder_2_f), .g(_7decoder_2_g));
  _5bit_2x1_multiplexer _2x1_mult (
    .A(A), .B(_5bit_subtractor_output), .Seletor(_5it_comparator_a___b), .out_4(_2x1_mult_out_4));
  _5bit_subtractor _5bit_subtractor (
    .\output (_5bit_subtractor_output), .m(_1), .A(A), .B(_01010_2));  // open: Overflow
  _5bit_comparator _5bit_comparator (
    .left_less(in_30), .left_greater(in_30), .left_equal(_1_7), .A___B(_5bit_comparator_a___b), .A(B),
    .B(_01010_2));  // open: A___B_2, A___B_3
  _5bit_2x1_multiplexer _2x1_mult_2 (
    .A(B), .B(_5bit_sub_output), .Seletor(_5bit_comparator_a___b), .out_4(_2x1_mult_2_out_4));
  _7_Segment_Display u_7_segment_display_3 (
    .g(_7_decoder_g), .f(_7_decoder_f), .a(_7_decoder_a_2), .b(_7_decoder_b_2), .e(_7_decoder_e),
    .d(_7_decoder_d_2), .c(_7_decoder_c_2));  // open: dp
  _7_Segment_Display u_7_segment_display_4 (
    .g(_7decoder_2_g), .f(_7decoder_2_f), .a(_7decoder_2_a_2), .b(_7decoder_2_b_2), .e(_7decoder_2_e),
    .d(_7decoder_2_d_2), .c(_7decoder_2_c_2));  // open: dp
  _7_segment_decoder _7decoder_3 (
    .A(_2x1_mult_out_4[3]), .B(_2x1_mult_out_4[2]), .C(_2x1_mult_out_4[1]), .D(_2x1_mult_out_4[0]),
    .a_2(_7decoder_3_a_2), .b_2(_7decoder_3_b_2), .c_2(_7decoder_3_c_2), .d_2(_7decoder_3_d_2),
    .e(_7decoder_3_e), .f(_7decoder_3_f), .g(_7decoder_3_g));
  _5bit_comparator _5it_comparator (
    .left_less(in_4), .left_greater(in_5), .left_equal(_1), .A___B(_5it_comparator_a___b), .A(A), .B(_01010_2));  // open: A___B_2, A___B_3
  _7_segment_decoder _7_decoder (
    .A(_2x1_mult_2_out_4[3]), .B(_2x1_mult_2_out_4[2]), .C(_2x1_mult_2_out_4[1]), .D(_2x1_mult_2_out_4[0]),
    .a_2(_7_decoder_a_2), .b_2(_7_decoder_b_2), .c_2(_7_decoder_c_2), .d_2(_7_decoder_d_2), .e(_7_decoder_e),
    .f(_7_decoder_f), .g(_7_decoder_g));
  multiplier multiplier_1 (.Input(A), .aux(_0_3), .Output(multiplier_1_output), .overflow(multiplier_1_overflow));
  shift_bit_n_times shift_bit_n_times_1 (
    .A(A), .B(B), .aux(aux), .bit_aux(_1_8), .\output (shift_bit_n_times_1_output));
  not not_3 (not_3_out, in_3[1]);
  and and_1 (and_1_out, in_3[2], not_3_out, in_3[0]);
  and and_2 (and_2_out, and_1_out, multiplier_1_overflow);
  C2_format C2_format (.Input(A), .Aux(_0), .Output(C2_format_output));
  greater_than greater_than (
    .left_less(in_9), .left_greater(in_8), .left_equal(_1_2), .out_6(greater_than_out_6), .A(A), .B(B),
    .Output(greater_than_output));
  less_or_equal_to less_or_equal_to (
    .left_less(in_13), .left_greater(in_12), .left_equal(_1_3), .out_7(less_or_equal_to_out_7), .A(A), .B(B),
    .\output (less_or_equal_to_output));
  min min (.left_less(in_25), .left_greater(in_24), .left_equal(_1_6), .A(A), .B(B), .out_6(min_out_6));
  _5bit_subtractor subtractor (.\output (subtractor_output), .m(_1_9), .Overflow(subtractor_overflow), .A(A), .B(B));
  _5bit_adder adder (.\output (adder_output), .m(_0_5), .Overflow(adder_overflow), .A(A), .B(B));
  and and_3 (and_3_out, greater_than_out_6, and_5_out);
  and and_4 (and_4_out, less_or_equal_to_out_7, and_6_out);
  and and_5 (and_5_out, in_3[2], not_5_out, not_4_out);
  not not_4 (not_4_out, in_3[0]);
  not not_5 (not_5_out, in_3[1]);
  LED LED_OVERFLOW (.in(or_1_out));
  or or_1 (or_1_out, subtractor_overflow, and_2_out, adder_overflow);
  and and_6 (and_6_out, in_3[1], not_6_out, in_3[0]);
  not not_6 (not_6_out, in_3[2]);
  _5bit_8x1_multiplexer _8x1_mult (
    .A(shift_bit_n_times_1_output), .B(C2_format_output), .C(multiplier_1_output), .D(greater_than_output),
    .E(less_or_equal_to_output), .F(min_out_6), .G(subtractor_output), .H(adder_output), .Seletor(in_3),
    .out_10(_8x1_mult_out_10));
  or or_2 (or_2_out, and_3_out, and_4_out);
  LED LED_STATUS (.in(or_2_out));
  C2_format C2_format_2 (.Input(_8x1_mult_out_10), .Aux(in_19), .Output(C2_format_2_output));
  _5bit_comparator _5bt_comparator (
    .left_less(in_20), .left_greater(in_19), .left_equal(_1_4), .A___B(_5bt_comparator_a___b),
    .A(C2_format_2_output), .B(_01010));  // open: A___B_2, A___B_3
  _5bit_2x1_multiplexer _2x1mult (
    .A(C2_format_2_output), .B(subtractor_2_output), .Seletor(_5bt_comparator_a___b), .out_4(out_33));
  not not_7 (not_7_out, _5bt_comparator_a___b);
  _7_segment_decoder _7_decoder_2 (
    .A(_0_4), .B(_0_4), .C(_0_4), .D(not_7_out), .a_2(_7_decoder_2_a_2), .b_2(_7_decoder_2_b_2),
    .c_2(_7_decoder_2_c_2), .d_2(_7_decoder_2_d_2), .e(_7_decoder_2_e), .f(_7_decoder_2_f), .g(_7_decoder_2_g));
  _7_Segment_Display u_7_segment_display_5 (
    .g(n7_segment_decoder_1_g), .f(n7_segment_decoder_1_f), .a(n7_segment_decoder_1_a_2),
    .b(n7_segment_decoder_1_b_2), .e(n7_segment_decoder_1_e), .d(n7_segment_decoder_1_d_2),
    .c(n7_segment_decoder_1_c_2));  // open: dp
  _7_Segment_Display u_7_segment_display_6 (
    .g(_7_decoder_2_g), .f(_7_decoder_2_f), .a(_7_decoder_2_a_2), .b(_7_decoder_2_b_2), .e(_7_decoder_2_e),
    .d(_7_decoder_2_d_2), .c(_7_decoder_2_c_2));  // open: dp
  _5bit_subtractor subtractor_2 (
    .\output (subtractor_2_output), .m(_1_5), .A(C2_format_2_output), .B(_01010));  // open: Overflow
  LED LED_NEGATIVO (.in(_8x1_mult_out_10[4]));
  _7_segment_decoder u_7_segment_decoder_1 (
    .A(out_33[3]), .B(out_33[2]), .C(out_33[1]), .D(out_33[0]), .a_2(n7_segment_decoder_1_a_2),
    .b_2(n7_segment_decoder_1_b_2), .c_2(n7_segment_decoder_1_c_2), .d_2(n7_segment_decoder_1_d_2),
    .e(n7_segment_decoder_1_e), .f(n7_segment_decoder_1_f), .g(n7_segment_decoder_1_g));

  // Notes on the sheet:
  //   7 decoder
endmodule

module half_adder (
  input  A,
  input  B,
  output Carry_out,
  output Soma
);

  and and_1 (Carry_out, B, A);
  xor xor_1 (Soma, A, B);
endmodule

module full_adder (
  input  A,
  input  B,
  input  Carry_in,
  output Carry_out,
  output Soma
);

  wire half_adder_2_carry_out, half_adder_carry_out, half_adder_soma;

  half_adder half_adder (.A(A), .B(B), .Carry_out(half_adder_carry_out), .Soma(half_adder_soma));
  half_adder half_adder_2 (.A(half_adder_soma), .B(Carry_in), .Carry_out(half_adder_2_carry_out), .Soma(Soma));
  or or_1 (Carry_out, half_adder_carry_out, half_adder_2_carry_out);
endmodule

module C2_format (
  input  [4:0] Input,
  input  Aux,
  output [4:0] Output
);

  wire full_adder_1_carry_out, full_adder_2_carry_out, full_adder_3_carry_out, full_adder_4_carry_out,
       not_1_out, not_2_out, not_3_out, not_4_out, not_5_out, not_6_out, not_7_out, xor_1_out, xor_2_out,
       xor_3_out, xor_4_out, xor_5_out;

  not not_1 (not_1_out, Input[0]);
  not not_2 (not_2_out, Input[1]);
  not not_3 (not_3_out, Input[2]);
  not not_4 (not_4_out, Input[3]);
  not not_5 (not_5_out, Input[4]);
  not not_6 (not_6_out, Input[4]);
  not not_7 (not_7_out, not_6_out);
  xor xor_1 (xor_1_out, not_1_out, not_6_out);
  xor xor_2 (xor_2_out, not_2_out, not_6_out);
  xor xor_3 (xor_3_out, not_3_out, not_6_out);
  xor xor_4 (xor_4_out, not_4_out, not_6_out);
  xor xor_5 (xor_5_out, not_5_out, not_6_out);
  full_adder full_adder_1 (
    .A(xor_1_out), .B(not_7_out), .Carry_in(Aux), .Carry_out(full_adder_1_carry_out), .Soma(Output[0]));
  full_adder full_adder_2 (
    .A(xor_2_out), .B(Aux), .Carry_in(full_adder_1_carry_out), .Carry_out(full_adder_2_carry_out),
    .Soma(Output[1]));
  full_adder full_adder_3 (
    .A(xor_3_out), .B(Aux), .Carry_in(full_adder_2_carry_out), .Carry_out(full_adder_3_carry_out),
    .Soma(Output[2]));
  full_adder full_adder_4 (
    .A(xor_4_out), .B(Aux), .Carry_in(full_adder_3_carry_out), .Carry_out(full_adder_4_carry_out),
    .Soma(Output[3]));
  full_adder full_adder_5 (
    .A(xor_5_out), .B(Aux), .Carry_in(full_adder_4_carry_out), .Soma(Output[4]));  // open: Carry_out
endmodule

module _1bit_comparator (
  input  A,
  input  B,
  input  in_equal,
  input  in_greater_than,
  input  in_less_than,
  output A___B,
  output A___B_2,
  output A___B_3
);

  wire and_1_out, and_2_out, not_1_out, not_2_out, xnor_1_out;

  not not_1 (not_1_out, B);
  not not_2 (not_2_out, A);
  xnor xnor_1 (xnor_1_out, A, B);
  and and_1 (and_1_out, A, in_equal, not_1_out);
  and and_2 (and_2_out, not_2_out, in_equal, B);
  and and_3 (A___B, xnor_1_out, in_equal);
  or or_1 (A___B_2, in_greater_than, and_1_out);
  or or_2 (A___B_3, in_less_than, and_2_out);
endmodule

module _5bit_comparator (
  input  left_less,
  input  left_greater,
  input  left_equal,
  input  [4:0] A,
  input  [4:0] B,
  output A___B,
  output A___B_2,
  output A___B_3
);

  wire n1bit_comparator_1_a___b, n1bit_comparator_1_a___b_2, n1bit_comparator_1_a___b_3,
       n1bit_comparator_2_a___b, n1bit_comparator_2_a___b_2, n1bit_comparator_2_a___b_3,
       n1bit_comparator_3_a___b, n1bit_comparator_3_a___b_2, n1bit_comparator_3_a___b_3,
       n1bit_comparator_4_a___b, n1bit_comparator_4_a___b_2, n1bit_comparator_4_a___b_3, not_1_out, not_2_out;

  _1bit_comparator u_1bit_comparator_1 (
    .A(not_2_out), .B(not_1_out), .in_equal(left_equal), .in_greater_than(left_greater),
    .in_less_than(left_less), .A___B(n1bit_comparator_1_a___b), .A___B_2(n1bit_comparator_1_a___b_2),
    .A___B_3(n1bit_comparator_1_a___b_3));
  _1bit_comparator u_1bit_comparator_2 (
    .A(A[3]), .B(B[3]), .in_equal(n1bit_comparator_1_a___b), .in_greater_than(n1bit_comparator_1_a___b_2),
    .in_less_than(n1bit_comparator_1_a___b_3), .A___B(n1bit_comparator_2_a___b),
    .A___B_2(n1bit_comparator_2_a___b_2), .A___B_3(n1bit_comparator_2_a___b_3));
  _1bit_comparator u_1bit_comparator_3 (
    .A(A[2]), .B(B[2]), .in_equal(n1bit_comparator_2_a___b), .in_greater_than(n1bit_comparator_2_a___b_2),
    .in_less_than(n1bit_comparator_2_a___b_3), .A___B(n1bit_comparator_3_a___b),
    .A___B_2(n1bit_comparator_3_a___b_2), .A___B_3(n1bit_comparator_3_a___b_3));
  _1bit_comparator u_1bit_comparator_4 (
    .A(A[1]), .B(B[1]), .in_equal(n1bit_comparator_3_a___b), .in_greater_than(n1bit_comparator_3_a___b_2),
    .in_less_than(n1bit_comparator_3_a___b_3), .A___B(n1bit_comparator_4_a___b),
    .A___B_2(n1bit_comparator_4_a___b_2), .A___B_3(n1bit_comparator_4_a___b_3));
  not not_1 (not_1_out, B[4]);
  not not_2 (not_2_out, A[4]);
  _1bit_comparator u_1bit_comparator_5 (
    .A(A[0]), .B(B[0]), .in_equal(n1bit_comparator_4_a___b), .in_greater_than(n1bit_comparator_4_a___b_2),
    .in_less_than(n1bit_comparator_4_a___b_3), .A___B(A___B_3), .A___B_2(A___B_2), .A___B_3(A___B));
endmodule

module _5bit_adder (
  input  m,
  input  [4:0] A,
  input  [4:0] B,
  output [4:0] \output ,
  output Overflow
);

  wire full_adder_1_carry_out, full_adder_2_carry_out, full_adder_3_carry_out, full_adder_4_carry_out,
       full_adder_5_carry_out;

  full_adder full_adder_1 (
    .A(A[4]), .B(B[4]), .Carry_in(full_adder_2_carry_out), .Carry_out(full_adder_1_carry_out),
    .Soma(\output [4]));
  xor xor_1 (Overflow, full_adder_2_carry_out, full_adder_1_carry_out);
  full_adder full_adder_2 (
    .A(A[3]), .B(B[3]), .Carry_in(full_adder_3_carry_out), .Carry_out(full_adder_2_carry_out),
    .Soma(\output [3]));
  full_adder full_adder_3 (
    .A(A[2]), .B(B[2]), .Carry_in(full_adder_5_carry_out), .Carry_out(full_adder_3_carry_out),
    .Soma(\output [2]));
  full_adder full_adder_4 (.A(A[0]), .B(B[0]), .Carry_in(m), .Carry_out(full_adder_4_carry_out), .Soma(\output [0]));
  full_adder full_adder_5 (
    .A(A[1]), .B(B[1]), .Carry_in(full_adder_4_carry_out), .Carry_out(full_adder_5_carry_out),
    .Soma(\output [1]));
endmodule

module _5bit_subtractor (
  input  m,
  input  [4:0] A,
  input  [4:0] B,
  output [4:0] \output ,
  output Overflow
);

  wire full_adder_1_carry_out, full_adder_2_carry_out, full_adder_3_carry_out, full_adder_4_carry_out,
       full_adder_5_carry_out, xor_2_out, xor_3_out, xor_4_out, xor_5_out, xor_6_out;

  xor xor_1 (Overflow, full_adder_1_carry_out, full_adder_2_carry_out);
  full_adder full_adder_1 (
    .A(A[3]), .B(xor_5_out), .Carry_in(full_adder_3_carry_out), .Carry_out(full_adder_1_carry_out),
    .Soma(\output [3]));
  full_adder full_adder_2 (
    .A(A[4]), .B(xor_6_out), .Carry_in(full_adder_1_carry_out), .Carry_out(full_adder_2_carry_out),
    .Soma(\output [4]));
  full_adder full_adder_3 (
    .A(A[2]), .B(xor_4_out), .Carry_in(full_adder_5_carry_out), .Carry_out(full_adder_3_carry_out),
    .Soma(\output [2]));
  full_adder full_adder_4 (
    .A(A[0]), .B(xor_2_out), .Carry_in(m), .Carry_out(full_adder_4_carry_out), .Soma(\output [0]));
  full_adder full_adder_5 (
    .A(A[1]), .B(xor_3_out), .Carry_in(full_adder_4_carry_out), .Carry_out(full_adder_5_carry_out),
    .Soma(\output [1]));
  xor xor_2 (xor_2_out, B[0], m);
  xor xor_3 (xor_3_out, B[1], m);
  xor xor_4 (xor_4_out, B[2], m);
  xor xor_5 (xor_5_out, B[3], m);
  xor xor_6 (xor_6_out, B[4], m);
endmodule

module min (
  input  left_less,
  input  left_greater,
  input  left_equal,
  input  [4:0] A,
  input  [4:0] B,
  output [4:0] out_6
);

  wire and_1_out, n5bit_comparator_1_a___b, n5bit_comparator_1_a___b_2, n5bit_comparator_1_a___b_3,
       not_1_out, or_1_out;

  not not_1 (not_1_out, n5bit_comparator_1_a___b);
  and and_1 (and_1_out, not_1_out, or_1_out);
  _5bit_comparator u_5bit_comparator_1 (
    .left_less(left_less), .left_greater(left_greater), .left_equal(left_equal),
    .A___B(n5bit_comparator_1_a___b), .A___B_2(n5bit_comparator_1_a___b_2),
    .A___B_3(n5bit_comparator_1_a___b_3), .A(A), .B(B));
  or or_1 (or_1_out, n5bit_comparator_1_a___b_2, n5bit_comparator_1_a___b_3);
  _5bit_2x1_multiplexer u_5bit_2x1_multiplexer_1 (.A(B), .B(A), .Seletor(and_1_out), .out_4(out_6));
endmodule

module _2x1_multiplexer (
  input  A,
  input  B,
  input  Seletor,
  output out_4
);

  wire and_1_out, and_2_out, not_1_out;

  not not_1 (not_1_out, Seletor);
  and and_1 (and_1_out, A, not_1_out);
  and and_2 (and_2_out, Seletor, B);
  or or_1 (out_4, and_1_out, and_2_out);
endmodule

module _5bit_2x1_multiplexer (
  input  [4:0] A,
  input  [4:0] B,
  input  Seletor,
  output [4:0] out_4
);

  wire not_1_out;

  not not_1 (not_1_out, Seletor);
  _2x1_multiplexer u_2x1_multiplexer_1 (.A(A[0]), .B(B[0]), .Seletor(not_1_out), .out_4(out_4[0]));
  _2x1_multiplexer u_2x1_multiplexer_2 (.A(A[1]), .B(B[1]), .Seletor(not_1_out), .out_4(out_4[1]));
  _2x1_multiplexer u_2x1_multiplexer_3 (.A(A[2]), .B(B[2]), .Seletor(not_1_out), .out_4(out_4[2]));
  _2x1_multiplexer u_2x1_multiplexer_4 (.A(A[3]), .B(B[3]), .Seletor(not_1_out), .out_4(out_4[3]));
  _2x1_multiplexer u_2x1_multiplexer_5 (.A(A[4]), .B(B[4]), .Seletor(not_1_out), .out_4(out_4[4]));
endmodule

module _5bit_4x1_multiplexer (
  input  Seletor1,
  input  Seletor2,
  input  [4:0] A,
  input  [4:0] B,
  input  [4:0] C,
  input  [4:0] D,
  output [4:0] out_7
);

  wire [4:0] n5bit_2x1_multiplexer_1_out_4, n5bit_2x1_multiplexer_2_out_4;

  _5bit_2x1_multiplexer u_5bit_2x1_multiplexer_1 (
    .A(A), .B(B), .Seletor(Seletor1), .out_4(n5bit_2x1_multiplexer_1_out_4));
  _5bit_2x1_multiplexer u_5bit_2x1_multiplexer_2 (
    .A(C), .B(D), .Seletor(Seletor1), .out_4(n5bit_2x1_multiplexer_2_out_4));
  _5bit_2x1_multiplexer u_5bit_2x1_multiplexer_3 (
    .A(n5bit_2x1_multiplexer_1_out_4), .B(n5bit_2x1_multiplexer_2_out_4), .Seletor(Seletor2), .out_4(out_7));
endmodule

module _5bit_8x1_multiplexer (
  input  [2:0] Seletor,
  input  [4:0] A,
  input  [4:0] B,
  input  [4:0] C,
  input  [4:0] D,
  input  [4:0] E,
  input  [4:0] F,
  input  [4:0] G,
  input  [4:0] H,
  output [4:0] out_10
);

  wire [4:0] n5bit_4x1_multiplexer_1_out_7, n5bit_4x1_multiplexer_2_out_7;

  _5bit_4x1_multiplexer u_5bit_4x1_multiplexer_1 (
    .A(A), .B(B), .C(C), .D(D), .Seletor1(Seletor[0]), .Seletor2(Seletor[1]),
    .out_7(n5bit_4x1_multiplexer_1_out_7));
  _5bit_4x1_multiplexer u_5bit_4x1_multiplexer_2 (
    .A(E), .B(F), .C(G), .D(H), .Seletor1(Seletor[0]), .Seletor2(Seletor[1]),
    .out_7(n5bit_4x1_multiplexer_2_out_7));
  _5bit_2x1_multiplexer u_5bit_2x1_multiplexer_1 (
    .A(n5bit_4x1_multiplexer_1_out_7), .B(n5bit_4x1_multiplexer_2_out_7), .Seletor(Seletor[2]), .out_4(out_10));
endmodule

module less_or_equal_to (
  input  left_less,
  input  left_equal,
  input  left_greater,
  input  [4:0] A,
  input  [4:0] B,
  output [4:0] \output ,
  output out_7
);

  wire n5bit_comparator_1_a___b, n5bit_comparator_1_a___b_3;

  _5bit_comparator u_5bit_comparator_1 (
    .left_less(left_less), .left_greater(left_greater), .left_equal(left_equal),
    .A___B(n5bit_comparator_1_a___b), .A___B_3(n5bit_comparator_1_a___b_3), .A(A), .B(B));  // open: A___B_2
  or or_1 (out_7, n5bit_comparator_1_a___b, n5bit_comparator_1_a___b_3);

  assign \output  = A;
endmodule

module greater_than (
  input  left_less,
  input  left_equal,
  input  left_greater,
  input  [4:0] A,
  input  [4:0] B,
  output out_6,
  output [4:0] Output
);

  _5bit_comparator u_5bit_comparator_1 (
    .left_less(left_less), .left_greater(left_greater), .left_equal(left_equal), .A___B_2(out_6), .A(A), .B(B));  // open: A___B, A___B_3

  assign Output = A;
endmodule

module _7_segment_decoder (
  input  A,
  input  B,
  input  C,
  input  D,
  output a_2,
  output b_2,
  output c_2,
  output d_2,
  output e,
  output f,
  output g
);

  wire and_1_out, and_2_out, and_3_out, and_4_out, and_5_out, and_6_out, and_7_out, and_8_out, and_9_out,
       and_10_out, not_1_out, not_2_out, not_3_out, xnor_1_out, xnor_2_out, xor_1_out;

  not not_1 (not_1_out, B);
  not not_2 (not_2_out, C);
  not not_3 (not_3_out, D);
  and and_1 (and_1_out, C, not_3_out);
  and and_2 (and_2_out, not_1_out, C);
  and and_3 (and_3_out, not_1_out, not_3_out);
  and and_4 (and_4_out, B, not_2_out, D);
  and and_5 (and_5_out, C, not_3_out);
  and and_6 (and_6_out, not_1_out, not_3_out);
  and and_7 (and_7_out, not_2_out, not_3_out);
  and and_8 (and_8_out, B, not_3_out);
  and and_9 (and_9_out, B, not_2_out);
  xor xor_1 (xor_1_out, B, C);
  and and_10 (and_10_out, B, not_3_out);
  xnor xnor_1 (xnor_1_out, B, D);
  xnor xnor_2 (xnor_2_out, C, D);
  or or_1 (a_2, A, C, xnor_1_out);
  or or_2 (b_2, not_1_out, xnor_2_out);
  or or_3 (c_2, not_2_out, D, B);
  or or_4 (d_2, and_1_out, and_2_out, and_3_out, and_4_out);
  or or_5 (e, and_5_out, and_6_out);
  or or_6 (f, and_7_out, and_8_out, A, and_9_out);
  or or_7 (g, xor_1_out, A, and_10_out);
endmodule

module shift_bit (
  input  in_1,
  input  [4:0] A,
  output [4:0] S
);

  wire and_2_out, and_3_out, and_4_out, and_5_out, and_6_out, and_7_out, and_8_out, and_9_out, not_1_out;

  not not_1 (not_1_out, in_1);
  and and_1 (S[0], not_1_out, A[0]);
  and and_2 (and_2_out, A[1], not_1_out);
  and and_3 (and_3_out, A[0], in_1);
  and and_4 (and_4_out, A[2], not_1_out);
  and and_5 (and_5_out, in_1, A[1]);
  and and_6 (and_6_out, A[3], not_1_out);
  and and_7 (and_7_out, in_1, A[2]);
  and and_8 (and_8_out, A[4], not_1_out);
  and and_9 (and_9_out, in_1, A[3]);
  or or_1 (S[1], and_2_out, and_3_out);
  or or_2 (S[2], and_4_out, and_5_out);
  or or_3 (S[3], and_6_out, and_7_out);
  or or_4 (S[4], and_8_out, and_9_out);
endmodule

module shift_bit_n_times (
  input  [4:0] aux,
  input  [4:0] A,
  input  [4:0] B,
  input  bit_aux,
  output [4:0] \output 
);

  wire and_1_out, not_1_out, or_1_out;
  wire [4:0] add_one_1_output, add_one_2_output, add_one_3_output, add_one_4_output, add_one_5_output,
       add_one_6_output, add_one_7_output, add_one_8_output, add_one_9_output, add_one_10_output,
       add_one_11_output, add_one_12_output, add_one_13_output, add_one_14_output, shift_aux_1_out_6,
       shift_aux_2_out_6, shift_aux_3_out_6, shift_aux_4_out_6, shift_aux_5_out_6, shift_aux_6_out_6,
       shift_aux_7_out_6, shift_aux_9_out_6, shift_aux_10_out_6, shift_aux_11_out_6, shift_aux_12_out_6,
       shift_aux_13_out_6, shift_aux_14_out_6, shift_bit_1_s;

  or or_1 (or_1_out, B[0], B[1], B[2], B[3], B[4]);
  not not_1 (not_1_out, bit_aux);
  and and_1 (and_1_out, or_1_out, bit_aux);
  shift_bit shift_bit_1 (.A(A), .in_1(and_1_out), .S(shift_bit_1_s));
  add_one add_one_1 (.Input(add_one_14_output), .Aux(not_1_out), .Output(add_one_1_output));
  add_one add_one_2 (.Input(aux), .Aux(not_1_out), .Output(add_one_2_output));
  shift_aux shift_aux_1 (
    .B(B), .A(shift_bit_1_s), .current(add_one_2_output), .in_4(not_1_out), .in_5(bit_aux),
    .out_6(shift_aux_1_out_6));
  shift_aux shift_aux_2 (
    .B(B), .A(shift_aux_14_out_6), .current(add_one_1_output), .in_4(not_1_out), .in_5(bit_aux),
    .out_6(shift_aux_2_out_6));
  add_one add_one_3 (.Input(add_one_2_output), .Aux(not_1_out), .Output(add_one_3_output));
  add_one add_one_4 (.Input(add_one_1_output), .Aux(not_1_out), .Output(add_one_4_output));
  shift_aux shift_aux_3 (
    .B(B), .A(shift_aux_2_out_6), .current(add_one_4_output), .in_4(not_1_out), .in_5(bit_aux),
    .out_6(shift_aux_3_out_6));
  shift_aux shift_aux_4 (
    .B(B), .A(shift_aux_1_out_6), .current(add_one_3_output), .in_4(not_1_out), .in_5(bit_aux),
    .out_6(shift_aux_4_out_6));
  add_one add_one_5 (.Input(add_one_4_output), .Aux(not_1_out), .Output(add_one_5_output));
  add_one add_one_6 (.Input(add_one_3_output), .Aux(not_1_out), .Output(add_one_6_output));
  shift_aux shift_aux_5 (
    .B(B), .A(shift_aux_4_out_6), .current(add_one_6_output), .in_4(not_1_out), .in_5(bit_aux),
    .out_6(shift_aux_5_out_6));
  shift_aux shift_aux_6 (
    .B(B), .A(shift_aux_3_out_6), .current(add_one_5_output), .in_4(not_1_out), .in_5(bit_aux),
    .out_6(shift_aux_6_out_6));
  add_one add_one_7 (.Input(add_one_6_output), .Aux(not_1_out), .Output(add_one_7_output));
  add_one add_one_8 (.Input(add_one_5_output), .Aux(not_1_out), .Output(add_one_8_output));
  shift_aux shift_aux_7 (
    .B(B), .A(shift_aux_5_out_6), .current(add_one_7_output), .in_4(not_1_out), .in_5(bit_aux),
    .out_6(shift_aux_7_out_6));
  shift_aux shift_aux_8 (
    .B(B), .A(shift_aux_6_out_6), .current(add_one_8_output), .in_4(not_1_out), .in_5(bit_aux),
    .out_6(\output ));
  add_one add_one_9 (.Input(add_one_7_output), .Aux(not_1_out), .Output(add_one_9_output));
  shift_aux shift_aux_9 (
    .B(B), .A(shift_aux_7_out_6), .current(add_one_9_output), .in_4(not_1_out), .in_5(bit_aux),
    .out_6(shift_aux_9_out_6));
  add_one add_one_10 (.Input(add_one_9_output), .Aux(not_1_out), .Output(add_one_10_output));
  shift_aux shift_aux_10 (
    .B(B), .A(shift_aux_9_out_6), .current(add_one_10_output), .in_4(not_1_out), .in_5(bit_aux),
    .out_6(shift_aux_10_out_6));
  add_one add_one_11 (.Input(add_one_10_output), .Aux(not_1_out), .Output(add_one_11_output));
  shift_aux shift_aux_11 (
    .B(B), .A(shift_aux_10_out_6), .current(add_one_11_output), .in_4(not_1_out), .in_5(bit_aux),
    .out_6(shift_aux_11_out_6));
  add_one add_one_12 (.Input(add_one_11_output), .Aux(not_1_out), .Output(add_one_12_output));
  shift_aux shift_aux_12 (
    .B(B), .A(shift_aux_11_out_6), .current(add_one_12_output), .in_4(not_1_out), .in_5(bit_aux),
    .out_6(shift_aux_12_out_6));
  add_one add_one_13 (.Input(add_one_12_output), .Aux(not_1_out), .Output(add_one_13_output));
  shift_aux shift_aux_13 (
    .B(B), .A(shift_aux_12_out_6), .current(add_one_13_output), .in_4(not_1_out), .in_5(bit_aux),
    .out_6(shift_aux_13_out_6));
  add_one add_one_14 (.Input(add_one_13_output), .Aux(not_1_out), .Output(add_one_14_output));
  shift_aux shift_aux_14 (
    .B(B), .A(shift_aux_13_out_6), .current(add_one_14_output), .in_4(not_1_out), .in_5(bit_aux),
    .out_6(shift_aux_14_out_6));
endmodule

module shift_aux (
  input  [4:0] B,
  input  [4:0] A,
  input  [4:0] current,
  input  in_4,
  input  in_5,
  output [4:0] out_6
);

  wire and_1_out, n5bit_comparator_1_a___b;

  _5bit_comparator u_5bit_comparator_1 (
    .left_less(in_4), .left_greater(in_4), .left_equal(in_5), .A___B(n5bit_comparator_1_a___b), .A(current),
    .B(B));  // open: A___B_2, A___B_3
  and and_1 (and_1_out, n5bit_comparator_1_a___b, in_5);
  shift_bit shift_bit_1 (.A(A), .in_1(and_1_out), .S(out_6));
endmodule

module add_one (
  input  [4:0] Input,
  input  Aux,
  output [4:0] Output
);

  wire full_adder_1_carry_out, full_adder_2_carry_out, full_adder_3_carry_out, full_adder_4_carry_out,
       not_1_out, xor_1_out, xor_2_out, xor_3_out, xor_4_out, xor_5_out;

  not not_1 (not_1_out, Input[4]);
  xor xor_1 (xor_1_out, Input[0], Input[4]);
  xor xor_2 (xor_2_out, Input[1], Input[4]);
  xor xor_3 (xor_3_out, Input[2], Input[4]);
  xor xor_4 (xor_4_out, Input[3], Input[4]);
  xor xor_5 (xor_5_out, Input[4], Input[4]);
  full_adder full_adder_1 (
    .A(xor_1_out), .B(not_1_out), .Carry_in(Aux), .Carry_out(full_adder_1_carry_out), .Soma(Output[0]));
  full_adder full_adder_2 (
    .A(xor_2_out), .B(Aux), .Carry_in(full_adder_1_carry_out), .Carry_out(full_adder_2_carry_out),
    .Soma(Output[1]));
  full_adder full_adder_3 (
    .A(xor_3_out), .B(Aux), .Carry_in(full_adder_2_carry_out), .Carry_out(full_adder_3_carry_out),
    .Soma(Output[2]));
  full_adder full_adder_4 (
    .A(xor_4_out), .B(Aux), .Carry_in(full_adder_3_carry_out), .Carry_out(full_adder_4_carry_out),
    .Soma(Output[3]));
  full_adder full_adder_5 (
    .A(xor_5_out), .B(Aux), .Carry_in(full_adder_4_carry_out), .Soma(Output[4]));  // open: Carry_out
endmodule

module multiplier (
  input  aux,
  input  [4:0] Input,
  output overflow,
  output [4:0] Output
);

  wire and_2_out, and_3_out, and_4_out, and_5_out, and_6_out, and_7_out, and_8_out, and_9_out, and_10_out,
       and_11_out, and_12_out, and_13_out, and_14_out, and_15_out, and_16_out, and_17_out, and_18_out,
       and_19_out, and_20_out, and_21_out, and_22_out, and_23_out, and_24_out, full_adder_1_carry_out,
       full_adder_1_soma, full_adder_2_carry_out, full_adder_2_soma, full_adder_3_carry_out,
       full_adder_3_soma, full_adder_4_carry_out, full_adder_4_soma, full_adder_5_carry_out,
       full_adder_5_soma, full_adder_6_carry_out, full_adder_6_soma, full_adder_7_carry_out,
       full_adder_7_soma, full_adder_8_carry_out, full_adder_8_soma, full_adder_9_carry_out,
       full_adder_9_soma, full_adder_10_carry_out, full_adder_10_soma, full_adder_11_carry_out,
       full_adder_11_soma, full_adder_12_carry_out, full_adder_12_soma, half_adder_1_carry_out,
       half_adder_2_carry_out, half_adder_3_carry_out, half_adder_4_carry_out, half_adder_4_soma,
       half_adder_5_carry_out, half_adder_5_soma, half_adder_6_carry_out, half_adder_6_soma,
       half_adder_7_carry_out, half_adder_7_soma, half_adder_8_carry_out, half_adder_8_soma;
  wire [4:0] c2_format_1_output;

  C2_format c2_format_1 (.Input(Input), .Aux(aux), .Output(c2_format_1_output));
  or or_1 (overflow, half_adder_8_soma, full_adder_12_soma, half_adder_5_soma, full_adder_10_soma, full_adder_11_soma);
  and and_1 (Output[0], c2_format_1_output[0], c2_format_1_output[0]);
  and and_2 (and_2_out, c2_format_1_output[0], c2_format_1_output[1]);
  half_adder half_adder_1 (.A(and_2_out), .B(and_2_out), .Carry_out(half_adder_1_carry_out), .Soma(Output[1]));
  and and_3 (and_3_out, c2_format_1_output[0], c2_format_1_output[2]);
  full_adder full_adder_1 (
    .A(and_3_out), .B(and_4_out), .Carry_in(half_adder_1_carry_out), .Carry_out(full_adder_1_carry_out),
    .Soma(full_adder_1_soma));
  and and_4 (and_4_out, c2_format_1_output[1], c2_format_1_output[1]);
  and and_5 (and_5_out, c2_format_1_output[2], c2_format_1_output[0]);
  half_adder half_adder_2 (.A(and_5_out), .B(full_adder_1_soma), .Carry_out(half_adder_2_carry_out), .Soma(Output[2]));
  and and_6 (and_6_out, c2_format_1_output[3], c2_format_1_output[0]);
  full_adder full_adder_2 (
    .A(and_6_out), .B(and_8_out), .Carry_in(full_adder_1_carry_out), .Carry_out(full_adder_2_carry_out),
    .Soma(full_adder_2_soma));
  and and_7 (and_7_out, c2_format_1_output[2], c2_format_1_output[1]);
  and and_8 (and_8_out, c2_format_1_output[2], c2_format_1_output[1]);
  full_adder full_adder_3 (
    .A(full_adder_2_soma), .B(and_7_out), .Carry_in(half_adder_2_carry_out),
    .Carry_out(full_adder_3_carry_out), .Soma(full_adder_3_soma));
  and and_9 (and_9_out, c2_format_1_output[4], c2_format_1_output[0]);
  and and_10 (and_10_out, c2_format_1_output[2], c2_format_1_output[2]);
  and and_11 (and_11_out, c2_format_1_output[3], c2_format_1_output[0]);
  half_adder half_adder_3 (.A(full_adder_3_soma), .B(and_11_out), .Carry_out(half_adder_3_carry_out), .Soma(Output[3]));
  and and_12 (and_12_out, c2_format_1_output[3], c2_format_1_output[1]);
  full_adder full_adder_4 (
    .A(and_9_out), .B(and_12_out), .Carry_in(full_adder_2_carry_out), .Carry_out(full_adder_4_carry_out),
    .Soma(full_adder_4_soma));
  and and_13 (and_13_out, c2_format_1_output[2], c2_format_1_output[3]);
  full_adder full_adder_5 (
    .A(and_10_out), .B(full_adder_4_soma), .Carry_in(full_adder_3_carry_out),
    .Carry_out(full_adder_5_carry_out), .Soma(full_adder_5_soma));
  and and_14 (and_14_out, c2_format_1_output[1], c2_format_1_output[3]);
  and and_15 (and_15_out, c2_format_1_output[0], c2_format_1_output[4]);
  and and_16 (and_16_out, c2_format_1_output[1], c2_format_1_output[4]);
  half_adder half_adder_4 (
    .A(full_adder_4_carry_out), .B(and_16_out), .Carry_out(half_adder_4_carry_out), .Soma(half_adder_4_soma));
  full_adder full_adder_6 (
    .A(and_13_out), .B(half_adder_4_soma), .Carry_in(full_adder_5_carry_out),
    .Carry_out(full_adder_6_carry_out), .Soma(full_adder_6_soma));
  and and_17 (and_17_out, c2_format_1_output[3], c2_format_1_output[2]);
  full_adder full_adder_7 (
    .A(full_adder_5_soma), .B(and_14_out), .Carry_in(half_adder_3_carry_out),
    .Carry_out(full_adder_7_carry_out), .Soma(full_adder_7_soma));
  half_adder half_adder_5 (
    .A(and_15_out), .B(full_adder_7_soma), .Carry_out(half_adder_5_carry_out), .Soma(half_adder_5_soma));
  and and_18 (and_18_out, c2_format_1_output[2], c2_format_1_output[4]);
  half_adder half_adder_6 (
    .A(and_18_out), .B(full_adder_6_carry_out), .Carry_out(half_adder_6_carry_out), .Soma(half_adder_6_soma));
  full_adder full_adder_8 (
    .A(and_17_out), .B(full_adder_6_soma), .Carry_in(full_adder_7_carry_out),
    .Carry_out(full_adder_8_carry_out), .Soma(full_adder_8_soma));
  and and_19 (and_19_out, c2_format_1_output[1], c2_format_1_output[4]);
  and and_20 (and_20_out, c2_format_1_output[3], c2_format_1_output[3]);
  full_adder full_adder_9 (
    .A(and_20_out), .B(full_adder_8_carry_out), .Carry_in(half_adder_6_soma),
    .Carry_out(full_adder_9_carry_out), .Soma(full_adder_9_soma));
  full_adder full_adder_10 (
    .A(and_19_out), .B(full_adder_8_soma), .Carry_in(half_adder_5_carry_out),
    .Carry_out(full_adder_10_carry_out), .Soma(full_adder_10_soma));
  and and_21 (and_21_out, c2_format_1_output[3], c2_format_1_output[4]);
  half_adder half_adder_7 (
    .A(full_adder_9_carry_out), .B(and_21_out), .Carry_out(half_adder_7_carry_out), .Soma(half_adder_7_soma));
  and and_22 (and_22_out, c2_format_1_output[4], c2_format_1_output[2]);
  full_adder full_adder_11 (
    .A(full_adder_9_soma), .B(and_22_out), .Carry_in(full_adder_10_carry_out),
    .Carry_out(full_adder_11_carry_out), .Soma(full_adder_11_soma));
  and and_23 (and_23_out, c2_format_1_output[3], c2_format_1_output[4]);
  full_adder full_adder_12 (
    .A(half_adder_7_soma), .B(and_23_out), .Carry_in(full_adder_11_carry_out),
    .Carry_out(full_adder_12_carry_out), .Soma(full_adder_12_soma));
  and and_24 (and_24_out, c2_format_1_output[4], c2_format_1_output[4]);
  half_adder half_adder_8 (
    .A(full_adder_12_carry_out), .B(and_24_out), .Carry_out(half_adder_8_carry_out), .Soma(half_adder_8_soma));

  assign Output[4] = aux;
endmodule

module _8to16bit (
  input  [7:0] in_1,
  output [15:0] out_2
);


  assign out_2 = {{9{in_1[7]}}, in_1[6:0]};
endmodule

module loop (
  input  in_1,
  output [3:0] out_2
);

  wire and_1_out, and_2_out, clock_1_out;

  Clock clock_1 (.out(clock_1_out));
  T_Flip_Flop t_ff_1 (.clk(clock_1_out), .T(in_1), .Q(out_2[0]));  // open: Qn, preset, reset, en
  T_Flip_Flop t_ff_2 (.clk(clock_1_out), .T(out_2[0]), .Q(out_2[1]));  // open: Qn, preset, reset, en
  and and_1 (and_1_out, out_2[1], out_2[0]);
  T_Flip_Flop t_ff_3 (.clk(clock_1_out), .T(and_1_out), .Q(out_2[2]));  // open: Qn, preset, reset, en
  and and_2 (and_2_out, out_2[2], and_1_out);
  T_Flip_Flop t_ff_4 (.clk(clock_1_out), .T(and_2_out), .Q(out_2[3]));  // open: Qn, preset, reset, en
endmodule

module _16bit_adder (
  input  [15:0] A,
  input  [15:0] B,
  output [15:0] out_3
);

  wire full_adder_1_carry_out, full_adder_2_carry_out, full_adder_3_carry_out, full_adder_4_carry_out,
       full_adder_5_carry_out, full_adder_6_carry_out, full_adder_7_carry_out, full_adder_8_carry_out,
       full_adder_9_carry_out, full_adder_10_carry_out, full_adder_11_carry_out, full_adder_12_carry_out,
       full_adder_13_carry_out, full_adder_14_carry_out, half_adder_1_carry_out;

  half_adder half_adder_1 (.A(A[0]), .B(B[0]), .Carry_out(half_adder_1_carry_out), .Soma(out_3[0]));
  full_adder full_adder_1 (
    .A(A[1]), .B(B[1]), .Carry_in(half_adder_1_carry_out), .Carry_out(full_adder_1_carry_out), .Soma(out_3[1]));
  full_adder full_adder_2 (
    .A(A[2]), .B(B[2]), .Carry_in(full_adder_1_carry_out), .Carry_out(full_adder_2_carry_out), .Soma(out_3[2]));
  full_adder full_adder_3 (
    .A(A[3]), .B(B[3]), .Carry_in(full_adder_2_carry_out), .Carry_out(full_adder_3_carry_out), .Soma(out_3[3]));
  full_adder full_adder_4 (
    .A(A[4]), .B(B[4]), .Carry_in(full_adder_3_carry_out), .Carry_out(full_adder_4_carry_out), .Soma(out_3[4]));
  full_adder full_adder_5 (
    .A(A[5]), .B(B[5]), .Carry_in(full_adder_4_carry_out), .Carry_out(full_adder_5_carry_out), .Soma(out_3[5]));
  full_adder full_adder_6 (
    .A(A[6]), .B(B[6]), .Carry_in(full_adder_5_carry_out), .Carry_out(full_adder_6_carry_out), .Soma(out_3[6]));
  full_adder full_adder_7 (
    .A(A[7]), .B(B[7]), .Carry_in(full_adder_6_carry_out), .Carry_out(full_adder_7_carry_out), .Soma(out_3[7]));
  full_adder full_adder_8 (
    .A(A[8]), .B(B[8]), .Carry_in(full_adder_7_carry_out), .Carry_out(full_adder_8_carry_out), .Soma(out_3[8]));
  full_adder full_adder_9 (
    .A(A[9]), .B(B[9]), .Carry_in(full_adder_8_carry_out), .Carry_out(full_adder_9_carry_out), .Soma(out_3[9]));
  full_adder full_adder_10 (
    .A(A[10]), .B(B[10]), .Carry_in(full_adder_9_carry_out), .Carry_out(full_adder_10_carry_out),
    .Soma(out_3[10]));
  full_adder full_adder_11 (
    .A(A[11]), .B(B[11]), .Carry_in(full_adder_10_carry_out), .Carry_out(full_adder_11_carry_out),
    .Soma(out_3[11]));
  full_adder full_adder_12 (
    .A(A[12]), .B(B[12]), .Carry_in(full_adder_11_carry_out), .Carry_out(full_adder_12_carry_out),
    .Soma(out_3[12]));
  full_adder full_adder_13 (
    .A(A[13]), .B(B[13]), .Carry_in(full_adder_12_carry_out), .Carry_out(full_adder_13_carry_out),
    .Soma(out_3[13]));
  full_adder full_adder_14 (
    .A(A[14]), .B(B[14]), .Carry_in(full_adder_13_carry_out), .Carry_out(full_adder_14_carry_out),
    .Soma(out_3[14]));
  full_adder full_adder_15 (
    .A(A[15]), .B(B[15]), .Carry_in(full_adder_14_carry_out), .Soma(out_3[15]));  // open: Carry_out
endmodule

module lsb_comarer (
  input  in_1,
  input  [15:0] in_2,
  output out_3
);

  and and_1 (out_3, in_2[0], in_1);
endmodule
